# Fritzing sketch sonar (saved by Fritzing 0.9.3b)
breadboards: 1

parts:
  Micro_bit1 = Microbit
  hc-sr1 = hc-sr04
  VCC1 = 4 x AAA Battery Mount

nets:
  GND: Micro_bit1.GND, hc-sr1.GND, VCC1.-
  N1: Micro_bit1.1, hc-sr1.Trig
  N2: Micro_bit1.2, hc-sr1.Echo
  N3: hc-sr1.VCC, VCC1.+

custom parts:
  Microbit: BBC Microbit Fritzing part
