# Fritzing sketch temperature_sensor_oled (saved by Fritzing 0.9.3b)
breadboards: 1

parts:
  J1 = male pin header, 3 pins [form="♂ (male)"]
  Squix1 = OLED 0.96" 128x64 I2C SSD1306
  Micro_bit1 = Microbit

nets:
  N1: J1.pin1, Squix1.VCC, Micro_bit1.3V
  N2: J1.pin2, Micro_bit1.0
  GND: J1.pin3, Squix1.GND, Micro_bit1.GND
  N3: Squix1.SCL, Micro_bit1.19
  N4: Squix1.SCA, Micro_bit1.20

custom parts:
  Microbit: BBC Microbit Fritzing part
