# Fritzing sketch oled (saved by Fritzing 0.9.3b)
breadboards: 1

parts:
  Micro_bit1 = Microbit
  Squix1 = OLED 0.96" 128x64 I2C SSD1306

nets:
  GND: Micro_bit1.GND, Squix1.GND
  N1: Micro_bit1.3V, Squix1.VCC
  N2: Micro_bit1.19, Squix1.SCL
  N3: Micro_bit1.20, Squix1.SCA

custom parts:
  Microbit: BBC Microbit Fritzing part
