# Fritzing sketch traffic_light (saved by Fritzing 0.9.3b)
breadboards: 1

parts:
  LED1 = smd LED [color="Green (555nm)" package="0805 [SMD]"]
  LED2 = smd LED [color="Yellow (595nm)" package="0805 [SMD]"]
  LED3 = smd LED [color="Red (633nm)" package="0805 [SMD]"]
  Micro_bit1 = Microbit
  R1 = Resistor [tolerance=±5% resistance=220 package="2512 [SMD]"]
  R2 = Resistor [tolerance=±5% resistance=220 package="2512 [SMD]"]
  R3 = Resistor [tolerance=±5% resistance=220 package="2512 [SMD]"]

nets:
  N1: LED1.cathode, R1.Pin_1
  N2: LED1.anode, LED2.anode, LED3.anode, Micro_bit1.GND
  N3: LED2.cathode, R2.Pin_1
  N4: LED3.cathode, R3.Pin_1
  N5: Micro_bit1.0, R3.Pin_0
  N6: Micro_bit1.1, R2.Pin_0
  N7: Micro_bit1.2, R1.Pin_0

custom parts:
  Microbit: BBC Microbit Fritzing part
