# Fritzing sketch neopixel (saved by Fritzing 0.9.3b)
breadboards: 1

parts:
  U1 = NodeMCU V1.0
  LED1 = RGB LED - (4 legs) [package="5 mm [THT]"]

nets:
  N1: U1.D1, LED1.red_cathode
  N2: U1.3V3, LED1.common_anode
  N3: U1.GND, LED1.green_cathode

custom parts:
  NodeMCU V1.0: ESP8266 based NodeMCU
