# Fritzing sketch temperature_sensor (saved by Fritzing 0.9.3b)
breadboards: 1

parts:
  U1 = NodeMCU V1.0
  RHT1 = Humidity and Temperature Sensor RHT03
  R1 = Resistor [tolerance=±5% resistance=220 package=THT]

nets:
  N1: U1.D1, RHT1.Data-signal, R1.Pin_1
  3V3: U1.3V3, RHT1.Vcc, R1.Pin_0
  N2: U1.GND, RHT1.GND_2

custom parts:
  NodeMCU V1.0: ESP8266 based NodeMCU
